# Fritzing sketch client (saved by Fritzing 0.9.2b)
circuit board: 8.46667cm x 5.64444cm
breadboards: 1

parts:
  M1 = BMP280
  Part1 = Arduino Uno (Rev3)
  Mod1 = Dragino LoRa Shield V1.4
  Part2 = u-blox NEO-6M GPS Breakout
  Raspberry_Pi_Zero1 = Raspberry Pi Zero
  M2 = Humidity and Temperature Sensor DHT11

nets:
  5V: M1.VIN, Part1.5V, Mod1.5V@1, Part2.VCC, Raspberry_Pi_Zero1.5V, M2.Vcc
  GND: M1.GND, Part1.GND, Mod1.GND@1, Mod1.GND@2, Mod1.GND@3, Part2.GND, Raspberry_Pi_Zero1.GND, M2.GND
  N1: M1.SCL, Part1.A5/SCL, Mod1.A5, Mod1.SCL
  N2: M1.SDA, Part1.A4/SDA, Mod1.A4, Mod1.SDA
  N3: Part1.A0, Mod1.A0
  N4: Part1.A1, Mod1.A1
  N5: Part1.A2, Mod1.A2
  N6: Part1.A3, Mod1.A3
  N7: Part1.D8, Mod1.D8
  N8: Part1.D9_PWM, Mod1.D9
  N9: Part1.D10_PWM/SS, Mod1.D10
  N10: Part1.D11_PWM/MOSI, Mod1.D11
  N11: Part1.D12/MISO, Mod1.D12
  N12: Part1.D13/SCK, Mod1.D13
  N13: Part1.AREF, Mod1.AREF
  N14: Part1.D0/RX, Mod1.D0/Rx, Raspberry_Pi_Zero1.GIPO14
  N15: Part1.D1/TX, Mod1.D1/TX, Raspberry_Pi_Zero1.GIPO15
  N16: Part1.D2, Mod1.D2
  N17: Part1.D3_PWM, Mod1.D3, Part2.RXD
  N18: Part1.D4, Mod1.D4, Part2.TXD
  N19: Part1.D5_PWM, Mod1.D5, Mod1.D5@1, M2.Data
  N20: Part1.D6_PWM, Mod1.D6
  N21: Part1.D7, Mod1.D7
  N22: Part1.ioref, Mod1.IOREF
  N23: Part1.RESET, Mod1.RST
  3V3: Part1.3V3, Mod1.3V3
  VIN: Part1.VIN, Mod1.VIN
  N24: Part1.N/C, Mod1.N/C

custom parts:
  BMP280: Temperature Humidity Barometric presure Sensor, I2C
  Dragino LoRa Shield V1.4: Demonstration part that properly mounts on uno footprint boards in the Fritzing breadboard view
  Humidity and Temperature Sensor DHT11: Digital relative humidity & temperature sensor DHT11
